# Fritzing sketch DigitalCandle2 (saved by Fritzing 0.9.5d)
breadboards: 1

parts:
  パーツ2 = Arduino Uno (Rev3)
  パーツ3 = Adafruit MAX4466 Electret Microphone Amplifier [part_number="Adafruit #1063"]
  LED1 = LED - 5mm [color="Red (633nm)" package="5 mm [THT]"]
  R1 = Resistor [tolerance=±5% resistance=330 package=THT]

nets:
  N1: パーツ2.A0, パーツ3.OUT
  N2: パーツ2.D11_PWM/MOSI, R1.Pin_1
  3V3: パーツ2.3V3, パーツ3.VCC
  GND: パーツ2.GND, パーツ3.GND, LED1.cathode
  N3: LED1.anode, R1.Pin_0

custom parts:
  Adafruit MAX4466 Electret Microphone Amplifier: Add an ear to your project with this well-designed electret microphone amplifier. This fully assembled and tested board comes with a 20-20KHz electret microphone soldered on. For the amplification, we use the Maxim MAX4466, an op-amp specifically designed for this delicate task! The amplifier has excellent power supply noise rejection, so this amplifier sounds really good and isn't nearly as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
